# Fritzing sketch Pinmap ArduinoLidarBLE (saved by Fritzing 0.9.3b)
breadboards: 1

parts:
  Arduino_UNO = Arduino Uno (Rev3)
  Bluetooth_Module = Adafruit Bluefruit LE UART Friend [part_number="Adafruit #2479"]
  Sharp_2Y0A02 = Infrared Proximity Sensor

nets:
  N1: Arduino_UNO.A0, Sharp_2Y0A02.Vout
  N2: Arduino_UNO.D8, Bluetooth_Module.RTS
  N3: Arduino_UNO.D9_PWM, Bluetooth_Module.RXI
  N4: Arduino_UNO.D10_PWM/SS, Bluetooth_Module.TXO
  N5: Arduino_UNO.D11_PWM/MOSI, Bluetooth_Module.CTS
  N6: Arduino_UNO.D12/MISO, Bluetooth_Module.MODE
  N7: Arduino_UNO.D13/SCK, Bluetooth_Module.DFU
  GND: Arduino_UNO.GND, Bluetooth_Module.GND, Sharp_2Y0A02.GND
  3V3: Arduino_UNO.3V3, Bluetooth_Module.VIN
  5V: Arduino_UNO.5V, Sharp_2Y0A02.Vcc

custom parts:
  Adafruit Bluefruit LE UART Friend: The Bluefruit LE UART Friend makes it easy to add Bluetooth Low Energy connectivity to anything with a hardware or software serial port. We even have nice hardware flow control so you won't have to think about losing data. Connect to your Arduino or other microcontroller or even just a standard FTDI cable for debugging and testing.
